# Fritzing sketch FDD (saved by Fritzing 0.9.6b)
breadboards: 1

parts:
  Q2 = NPN-Transistor [package="TO92 [THT]"]
  R1 = Resistor [tolerance=±5% power=0.25 resistance=1k package=THT]
  Q1 = NPN-Transistor [package="TO92 [THT]"]
  R2 = Resistor [tolerance=±5% power=0.25 resistance=1k package=THT]
  Q3 = NPN-Transistor [package="TO92 [THT]"]
  R3 = Resistor [tolerance=±5% power=0.25 resistance=1k package=THT]

nets:
  N1: Q2.B, R2.Pin_0
  N2: Q2.C, Q1.C, Q3.C
  N3: R1.Pin_0, Q1.B
  N4: Q3.B, R3.Pin_0

notes:
  Direction
  Step
  Drive Select B
  FDD_DIR
  FDD_EN
  FDD_STEP
  GND
