# Fritzing sketch HDD (saved by Fritzing 0.9.6b)
breadboards: 1

parts:
  IC2 = L293D [package=THT]

nets:
  N1: IC2.Enable_1, IC2.Enable_2

notes:
  HDD 1 coil
  HDD 2 coil
  HDD B
  HDD A
  Pico's 3V3 output
  3.3V to 7V (you choose)
  HDD coil voltage
